# Fritzing sketch breadboard-fotswitch (saved by Fritzing 1.0.6)
breadboards: 1

parts:
  J1 = 3.5mm Switch Jack
  Pro_Micro1 = SparkFun Pro Micro
  R1 = Resistor [tolerance=±5% resistance=10k package="0805 [SMD]"]

nets:
  N1: J1.Pin_1, Pro_Micro1.GND
  N2: J1.Pin_3, Pro_Micro1.10, R1.Pin_1
  N3: Pro_Micro1.VCC, R1.Pin_0

custom parts:
  3.5mm Switch Jack: Distrelec Schweiz 3.5mm mono switching Jack
  SparkFun Pro Micro: The Pro Micro is similar to the Pro Mini except with an ATmega32U4 on board. The USB transceiver inside the 32U4 allows us to add USB connectivity on-board and do away with bulky external USB interface. Based on: https://github.com/unorthodox-engineers/unorthodox-arduino/blob/master/Unorthodox/fritzing/parts/Pro%20Micro.fzpz
